# Fritzing sketch arduino (saved by Fritzing 0.9.3b)
breadboards: 1

parts:
  Composant1 = Arduino Nano (Rev3.0)
  S1 = Round Pushbutton
  S2 = Round Pushbutton
  S3 = Round Pushbutton
  DFPlayer_Mini1 = DFPlayer MINI [package="DIP (Dual Inline) [THT]"]
  SP1 = SPEAKER [package=pcb_mount_speaker]
  R1 = Resistor [tolerance=±5% resistance=1k package=THT]

nets:
  N1: Composant1.GND, S1.leg0, S2.leg0, S3.leg0, DFPlayer_Mini1.GND#6
  N2: Composant1.D2, S2.leg1
  N3: Composant1.D3, S1.leg1
  N4: Composant1.D4, S3.leg1
  N5: Composant1.D10, DFPlayer_Mini1.TX
  N6: Composant1.D11/MOSI, R1.Pin_0
  5V: Composant1.5V, DFPlayer_Mini1.VCC
  N7: DFPlayer_Mini1.RX, R1.Pin_1
  N8: DFPlayer_Mini1.SPK1, SP1.-
  N9: DFPlayer_Mini1.SPK2, SP1.+

custom parts:
  DFPlayer MINI: MP3 module by DFRobot.com for playing Music from an SD-Card. Supports WAV and MP3 files.
